// Logisim project seq_ circuit.circ as structural Verilog: 1 circuit, main circuit main
module main (
  input  in_1,
  input  in_2,
  output out_3
);

  wire and_1_out, and_2_out, clock_1_out, d_ff_1_q, or_1_out, xor_1_out;

  xor xor_1 (xor_1_out, in_1, in_2);
  and and_1 (and_1_out, in_1, in_2);
  Clock clock_1 (.out(clock_1_out));
  xor xor_2 (out_3, xor_1_out, d_ff_1_q);
  and and_2 (and_2_out, xor_1_out, d_ff_1_q);
  D_Flip_Flop d_ff_1 (.clk(clock_1_out), .D(or_1_out), .Q(d_ff_1_q));  // open: Qn, preset, en, reset
  or or_1 (or_1_out, and_2_out, and_1_out);
endmodule
